# Fritzing sketch weather_station_atlas_indoor (saved by Fritzing 0.9.10b)
breadboards: 2

parts:
  Part31 = Adafruit BME680 [part_number="Adafruit #3660"]
  Part36 = Adafruit ItsyBitsy M4 [part_number="Adafruit #3800"]
  Part37 = Adafruit DS3231 [part_number="Adafruit #3013"]

nets:
  N1: Part31.SDI/SDA, Part36.D11
  VCC: Part31.VCC, Part36.+3V3, Part37.Vin
  N2: Part31.SCK/SCL, Part36.D13
  N3: Part31.SDO/ADR, Part36.D12
  N4: Part31.CS, Part36.D10
  GND: Part36.GND, Part37.GND
  N5: Part36.SCL, Part37.SCL
  N6: Part36.SDA, Part37.SDA

notes:
  DEVBOARD RX INSIDE
  USB CONNECTION TO
  COMPUTER
  Adafruit
  Itsy Bitsy M4
  Adafruit BME688 Temp/Humidity (indoors)

custom parts:
  Adafruit ItsyBitsy M4: What's smaller than a Feather but larger than a Trinket? It's an Adafruit ItsyBitsy M4 Express featuring the Microchip ATSAMD51! Small, powerful, with a ultra fast ATSAMD51 Cortex M4 processor running at 120 MHz - this microcontroller board is perfect when you want something very compact, with a ton of horsepower and a bunch of pins. This Itsy is like a bullet train, with it's 120MHz Cortex M4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
  Adafruit DS3231: The datasheet for the DS3231 explains that this part is an "Extremely Accurate I²C-Integrated RTC/TCXO/Crystal". And, hey, it does exactly what it says on the tin! This Real Time Clock (RTC) is the most precise you can get in a small, low power package. Most RTCs use an external 32kHz timing crystal that is used to keep time with low current draw. And that's all well and good, but those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
